// Logisim project GuessTheNumberXtreme.circ as structural Verilog: 3 circuits, main circuit main
module main (
  input  A3,
  input  A2,
  input  A1,
  input  A0
);

  Button dma ();  // open: out
  Hex_Digit_Display hex_digit_display_1 ();  // open: value, dp
  Hex_Digit_Display hex_digit_display_2 ();  // open: value, dp
  Button uma ();  // open: out
  Button dsa ();  // open: out
  Hex_Digit_Display hex_digit_display_3 ();  // open: value, dp
  Hex_Digit_Display hex_digit_display_4 (.value({A3, A2, A1, A0}));  // open: dp
  Button usa ();  // open: out
  Hex_Digit_Display hex_digit_display_5 ();  // open: value, dp
endmodule

module Flip_Flop_SR (
  input  Preset,
  input  S,
  input  Clock,
  input  Enable,
  input  Clear,
  output Q
);

  wire and_1_out, not_1_out;

  Adder adder_1 ();  // open: a, b, out, cin, cout
  S_R_Flip_Flop s_r_ff_1 (.S(S), .R(not_1_out), .clk(and_1_out), .Q(Q), .reset(Clear), .preset(Preset));  // open: Qn
  not not_1 (not_1_out, S);
  and and_1 (and_1_out, Clock, Enable);
endmodule

module Decrementar (
  input  in_1,
  input  in_2,
  input  in_3,
  input  Clock
);

  wire undriven, undriven_2;

  Flip_Flop_SR flip_flop_sr_1 (.Clock(Clock), .Enable(undriven));  // open: S, Preset, Clear, Q
  Flip_Flop_SR flip_flop_sr_2 (.Clock(Clock), .Enable(undriven_2));  // open: S, Preset, Clear, Q
  Flip_Flop_SR flip_flop_sr_3 (.Clock(Clock));  // open: S, Enable, Preset, Clear, Q
  Flip_Flop_SR flip_flop_sr_4 (.Clock(Clock));  // open: S, Enable, Preset, Clear, Q
endmodule
