// Logisim project Guess_The_Number_Xtreme.circ as structural Verilog: 12 circuits, main circuit main
// x
module main (
  input  in_1,
  input  in_2,
  input  in_3,
  input  in_4,
  input  in_5,
  input  in_6,
  input  in_7,
  input  in_8
);

  wire A_JOGANDO, A_VENCEU, ACERTOU, and_1_out, and_2_out, B_JOGANDO, B_VENCEU, CHUTANDO_X, CHUTANDO_Y,
       chutar, clock_1_out, clock_2_out, clock_3_out, clock_4_out, CONFIGURAR, dma_t, dmb_t, dsa_t, dsb_t,
       EMPATE, endA, endB, FIM_DE_JOGO, IGUAL, MAIOR, MENOR, proximo, RESET, SA, SB, START, STARTGAME, SX,
       SY, tunnel, uma_t, umb_t, usa_t, usb_t;
  wire [3:0] DMA, DMB, DSA, DSB, GA, GB, OA, OB, PA, PB, UMA, UMB, USA, USB, XH, YH;

  Button button_1 (.out(uma_t));
  Button button_2 (.out(dma_t));
  Hex_Digit_Display hex_digit_display_1 (.value(UMA));  // open: dp
  Hex_Digit_Display hex_digit_display_2 (.value(DMA));  // open: dp
  LED led_1 (.in(SA));
  Hex_Digit_Display hex_digit_display_3 (.value(PA));  // open: dp
  Button button_3 (.out(dsa_t));
  LED led_2 (.in(1'b1));
  LED led_3 (.in(1'b1));
  Hex_Digit_Display hex_digit_display_4 (.value(DSA));  // open: dp
  Hex_Digit_Display hex_digit_display_5 (.value(GA));  // open: dp
  LED led_4 (.in(A_JOGANDO));
  Button button_4 (.out(usa_t));
  Hex_Digit_Display hex_digit_display_6 (.value(USA));  // open: dp
  LED led_5 (.in(SX));
  LED led_6 (.in(A_VENCEU));
  Button button_5 (.out(START));
  LED led_7 (.in(MAIOR));
  Button button_6 (.out(proximo));
  Hex_Digit_Display hex_digit_display_7 (.value(XH));  // open: dp
  LED led_8 (.in(CHUTANDO_X));
  LED led_9 (.in(FIM_DE_JOGO));
  LED led_10 (.in(EMPATE));
  LED led_11 (.in(tunnel));
  Button button_7 (.out(CONFIGURAR));
  LED led_12 (.in(ACERTOU));
  LED led_13 (.in(IGUAL));
  Button button_8 (.out(chutar));
  LED led_14 (.in(SY));
  Hex_Digit_Display hex_digit_display_8 (.value(YH));  // open: dp
  LED led_15 (.in(CHUTANDO_Y));
  LED led_16 (.in(B_VENCEU));
  Button button_9 (.out(RESET));
  LED led_17 (.in(MENOR));
  Hex_Digit_Display hex_digit_display_9 (.value(DMB));  // open: dp
  Hex_Digit_Display hex_digit_display_10 (.value(PB));  // open: dp
  Button button_10 (.out(umb_t));
  Button button_11 (.out(dmb_t));
  LED led_18 (.in(1'b1));
  LED led_19 (.in(1'b1));
  Hex_Digit_Display hex_digit_display_11 (.value(UMB));  // open: dp
  LED led_20 (.in(SB));
  Hex_Digit_Display hex_digit_display_12 (.value(GB));  // open: dp
  LED led_21 (.in(B_JOGANDO));
  Button button_12 (.out(dsb_t));
  Button button_13 (.out(usb_t));
  Hex_Digit_Display hex_digit_display_13 (.value(DSB));  // open: dp
  Hex_Digit_Display hex_digit_display_14 (.value(USB));  // open: dp
  Coordenadas coordenadas_1 (
    .EndA(endA), .proximo(proximo), .chutar(chutar), .PlacarA(PA), .A_Venceu(A_VENCEU), .Empate(EMPATE),
    .B_venceu(B_VENCEU), .PlacarB(PB), .Acertou(ACERTOU), .MAIOR(MAIOR), .IGUAL(IGUAL), .MENOR(MENOR),
    .saidax(XH), .saiday(YH), .Jogador_A(A_JOGANDO), .Jogador_B(B_JOGANDO), .a(OA), .b(OB), .SX(SX), .SY(SY),
    .Chutando_X(CHUTANDO_X), .Chutando_Y(CHUTANDO_Y), .Fim_de_jogo(FIM_DE_JOGO), .EndB(endB), .endA_2(endA),
    .endB_2(endB), .start(START));
  Clock clock_1 (.out(clock_1_out));
  Clock clock_2 (.out(clock_2_out));
  numero_negativo Jogador_A (
    .Entrada_3(in_1), .Entrada_2(in_2), .Entrada_1(in_3), .Entrada_0(in_4), .original(OA), .negativo(SA),
    .\Saída (GA));
  numero_negativo Jogador_B (
    .Entrada_3(in_5), .Entrada_2(in_6), .Entrada_1(in_7), .Entrada_0(in_8), .original(OB), .negativo(SB),
    .\Saída (GB));
  cronometro cronometro_1 (
    .DMA(DMA), .UMA_2(UMA), .DSA_2(DSA), .USA_2(USA), .Clear(RESET), .Config(CONFIGURAR), .Start(START),
    .startGame(STARTGAME), .clkconfig(clock_1_out), .ConfigStatus(tunnel), .uda(dma_t), .uma(uma_t),
    .dsa(dsa_t), .EndTime(endA), .CLOCK(and_1_out), .usa(usa_t));
  and and_1 (and_1_out, A_JOGANDO, clock_3_out);
  cronometro cronometro_2 (
    .DMA(DMB), .UMA_2(UMB), .DSA_2(DSB), .USA_2(USB), .Clear(RESET), .Config(CONFIGURAR), .Start(START),
    .startGame(STARTGAME), .clkconfig(clock_2_out), .ConfigStatus(tunnel), .uda(dmb_t), .uma(umb_t),
    .dsa(dsb_t), .EndTime(endB), .CLOCK(and_2_out), .usa(usb_t));
  Clock clock_3 (.out(clock_3_out));
  and and_2 (and_2_out, B_JOGANDO, clock_4_out);
  Clock clock_4 (.out(clock_4_out));

  // Other names for the same wires on the sheet: A0 = in_4; A1 = in_3; A2 = in_2; A3 = in_1; B0 = in_8; B1 = in_7;
  //   B2 = in_6; B3 = in_5

  // Notes on the sheet:
  //   JOGADOR-A
  //   PLACAR
  //   JOGADOR-B
  //   PLACAR
endmodule

module Flip_Flop_SR (
  input  S_R,
  input  Clock,
  input  Preset,
  input  Enable,
  input  Clear,
  output out_6
);

  wire not_1_out;

  not not_1 (not_1_out, S_R);
  S_R_Flip_Flop s_r_ff_1 (
    .S(S_R), .clk(Clock), .R(not_1_out), .Q(out_6), .preset(Preset), .reset(Clear), .en(Enable));  // open: Qn
endmodule

module Decrementador (
  input  Clock,
  input  Preset,
  input  Enable,
  input  Clear,
  input  [3:0] valor_retorno,
  output [3:0] out_6
);

  wire comparator_1_eq;
  wire [3:0] adder_1_out, multiplexer_1_out;

  Hex_Digit_Display hex_digit_display_1 (.value(out_6));  // open: dp
  Flip_Flop_SR flip_flop_sr_1 (
    .S_R(multiplexer_1_out[3]), .Clock(Clock), .Preset(Preset), .Enable(Enable), .Clear(Clear),
    .out_6(out_6[3]));
  Flip_Flop_SR flip_flop_sr_2 (
    .S_R(multiplexer_1_out[2]), .Clock(Clock), .Preset(Preset), .Enable(Enable), .Clear(Clear),
    .out_6(out_6[2]));
  Flip_Flop_SR flip_flop_sr_3 (
    .S_R(multiplexer_1_out[1]), .Clock(Clock), .Preset(Preset), .Enable(Enable), .Clear(Clear),
    .out_6(out_6[1]));
  Multiplexer #(.width(4)) multiplexer_1 (
    .in0(adder_1_out), .in1(valor_retorno), .out(multiplexer_1_out), .sel(comparator_1_eq));  // open: en
  Flip_Flop_SR flip_flop_sr_4 (
    .S_R(multiplexer_1_out[0]), .Clock(Clock), .Preset(Preset), .Enable(Enable), .Clear(Clear),
    .out_6(out_6[0]));
  Hex_Digit_Display hex_digit_display_2 (.value(adder_1_out));  // open: dp
  Adder #(.width(4)) adder_1 (.a(out_6), .b(4'b1111), .out(adder_1_out));  // open: cin, cout
  Comparator #(.width(4)) comparator_1 (.a(adder_1_out), .b(4'b1111), .eq(comparator_1_eq));  // open: gt, lt
endmodule

module Verificador_9 (
  input  Enable
);

  wire and_1_out, clock_1_out, comparator_1_eq, comparator_2_eq, comparator_3_eq, comparator_4_eq, not_1_out;
  wire [3:0] and_2_out, decrementador_1_out_6, decrementador_2_out_6, decrementador_3_out_6,
       decrementador_4_out_6;

  and and_1 (and_1_out, Enable, not_1_out);
  not not_1 (not_1_out, comparator_2_eq);
  Hex_Digit_Display hex_digit_display_1 (.value(decrementador_1_out_6));  // open: dp
  Decrementador decrementador_1 (
    .Clock(comparator_1_eq), .Enable(and_1_out), .valor_retorno(4'b0101), .out_6(decrementador_1_out_6));  // open: Preset, Clear
  Hex_Digit_Display hex_digit_display_2 (.value(decrementador_2_out_6));  // open: dp
  Decrementador decrementador_2 (
    .Clock(comparator_3_eq), .Enable(and_1_out), .valor_retorno(4'b1001), .out_6(decrementador_2_out_6));  // open: Preset, Clear
  Comparator #(.width(4)) comparator_1 (.a(decrementador_2_out_6), .b(4'b1001), .eq(comparator_1_eq));  // open: gt, lt
  assign and_2_out = ~decrementador_1_out_6 & ~decrementador_2_out_6 & ~decrementador_3_out_6 & ~decrementador_4_out_6;  // AND_Gate and_2, 4 bits wide
  Hex_Digit_Display hex_digit_display_3 (.value(decrementador_3_out_6));  // open: dp
  Decrementador decrementador_3 (
    .Clock(comparator_4_eq), .Enable(and_1_out), .valor_retorno(4'b0101), .out_6(decrementador_3_out_6));  // open: Preset, Clear
  Comparator #(.width(4)) comparator_2 (.a(and_2_out), .b(4'b1111), .eq(comparator_2_eq));  // open: gt, lt
  Comparator #(.width(4)) comparator_3 (.a(decrementador_3_out_6), .b(4'b0101), .eq(comparator_3_eq));  // open: gt, lt
  Hex_Digit_Display hex_digit_display_4 (.value(decrementador_4_out_6));  // open: dp
  Decrementador decrementador_4 (
    .Clock(clock_1_out), .Enable(and_1_out), .valor_retorno(4'b1001), .out_6(decrementador_4_out_6));  // open: Preset, Clear
  Comparator #(.width(4)) comparator_4 (.a(decrementador_4_out_6), .b(4'b1001), .eq(comparator_4_eq));  // open: gt, lt
  Clock clock_1 (.out(clock_1_out));
endmodule

module decrementar_min_sec (
  input  Clear,
  input  Enable,
  input  usa,
  input  uma,
  input  dsa,
  input  uda,
  input  CLOCK,
  output [3:0] DMA,
  output [3:0] UMA_2,
  output [3:0] DSA_2,
  output [3:0] USA_2,
  output EndTime
);

  wire and_2_out, comparator_1_eq, comparator_2_eq, comparator_4_eq, multiplexer_1_out, multiplexer_2_out,
       multiplexer_3_out, multiplexer_4_out, not_1_out, not_2_out, or_1_out, or_2_out, or_3_out, or_4_out;
  wire [3:0] and_1_out;

  not not_1 (not_1_out, Enable);
  Hex_Digit_Display hex_digit_display_1 (.value(DMA));  // open: dp
  Decrementador decrementador_1 (
    .Clock(multiplexer_1_out), .Enable(or_1_out), .Clear(Clear), .valor_retorno(4'b0101), .out_6(DMA));  // open: Preset
  or or_1 (or_1_out, Enable, not_1_out);
  Multiplexer multiplexer_1 (.in0(uda), .in1(comparator_1_eq), .out(multiplexer_1_out), .sel(Enable));  // open: en
  Hex_Digit_Display hex_digit_display_2 (.value(UMA_2));  // open: dp
  Decrementador decrementador_2 (
    .Clock(multiplexer_2_out), .Enable(or_2_out), .Clear(Clear), .valor_retorno(4'b1001), .out_6(UMA_2));  // open: Preset
  or or_2 (or_2_out, Enable, not_1_out);
  Multiplexer multiplexer_2 (.in0(uma), .in1(comparator_2_eq), .out(multiplexer_2_out), .sel(Enable));  // open: en
  Comparator #(.width(4)) comparator_1 (.a(UMA_2), .b(4'b1001), .eq(comparator_1_eq));  // open: gt, lt
  assign and_1_out = ~DMA & ~UMA_2 & ~DSA_2 & ~USA_2;  // AND_Gate and_1, 4 bits wide
  Hex_Digit_Display hex_digit_display_3 (.value(DSA_2));  // open: dp
  Decrementador decrementador_3 (
    .Clock(multiplexer_3_out), .Enable(or_3_out), .Clear(Clear), .valor_retorno(4'b0101), .out_6(DSA_2));  // open: Preset
  or or_3 (or_3_out, Enable, not_1_out);
  Multiplexer multiplexer_3 (.in0(dsa), .in1(comparator_4_eq), .out(multiplexer_3_out), .sel(Enable));  // open: en
  Comparator #(.width(4)) comparator_2 (.a(DSA_2), .b(4'b0101), .eq(comparator_2_eq));  // open: gt, lt
  Comparator #(.width(4)) comparator_3 (.a(and_1_out), .b(4'b1111), .eq(EndTime));  // open: gt, lt
  Hex_Digit_Display hex_digit_display_4 (.value(USA_2));  // open: dp
  Decrementador decrementador_4 (
    .Clock(multiplexer_4_out), .Enable(or_4_out), .Clear(Clear), .valor_retorno(4'b1001), .out_6(USA_2));  // open: Preset
  or or_4 (or_4_out, Enable, not_1_out);
  Multiplexer multiplexer_4 (.in0(usa), .in1(and_2_out), .out(multiplexer_4_out), .sel(Enable));  // open: en
  Comparator #(.width(4)) comparator_4 (.a(USA_2), .b(4'b1001), .eq(comparator_4_eq));  // open: gt, lt
  and and_2 (and_2_out, not_2_out, CLOCK);
  Clock clock_1 (.out(CLOCK));
  not not_2 (not_2_out, EndTime);
endmodule

module Entrada (
  input  A3,
  input  A2,
  input  A1,
  input  A0,
  output [3:0] resultado
);

  Hex_Digit_Display hex_digit_display_1 (.value({A3, A2, A1, A0}));  // open: dp

  assign resultado = {A3, A2, A1, A0};
endmodule

// coordenadas
module Coordenadas (
  input  EndA,
  input  EndB,
  input  [3:0] a,
  input  [3:0] b,
  input  start,
  input  proximo,
  input  endA_2,
  input  endB_2,
  input  chutar,
  output [3:0] PlacarA,
  output A_Venceu,
  output Empate,
  output Fim_de_jogo,
  output B_venceu,
  output [3:0] PlacarB,
  output Jogador_A,
  output Jogador_B,
  output Acertou,
  output MAIOR,
  output IGUAL,
  output MENOR,
  output SX,
  output SY,
  output Chutando_Y,
  output Chutando_X,
  output [3:0] saidax,
  output [3:0] saiday
);

  wire and_1_out, and_2_out, and_3_out, and_4_out, and_5_out, and_6_out, and_7_out, and_8_out,
       comparator_1_eq, comparator_2_eq, comparator_3_eq, comparator_4_eq, comparator_5_eq, comparator_8_eq,
       comparator_8_gt, comparator_8_lt, comparator_9_eq, comparator_10_eq, comparator_12_eq,
       \teste_1_saída , verificador_jogador_1_out_3;
  wire [3:0] adder_1_out, adder_2_out, flip_flop_condicao_1_valor_saida, flip_flop_condicao_2_valor_saida,
       multiplexer_1_out, multiplexer_2_out, random_1_out, random_2_out, register_1_q, register_2_q;

  and and_1 (and_1_out, start, proximo);
  flip_flop_condicao flip_flop_condicao_1 (
    .Clock(and_1_out), .Preset(1'b0), .Enable(1'b1), .Clear(1'b0), .valor_retorno(4'b0000),
    .valor_max__1(4'b0011), .valor_saida(flip_flop_condicao_1_valor_saida));
  Hex_Digit_Display hex_digit_display_1 (.value(flip_flop_condicao_1_valor_saida));  // open: dp
  Comparator #(.width(4)) comparator_1 (
    .a(flip_flop_condicao_1_valor_saida), .b(4'b0010), .eq(comparator_1_eq));  // open: gt, lt
  Comparator #(.width(4)) comparator_2 (
    .a(flip_flop_condicao_1_valor_saida), .b(4'b0000), .eq(comparator_2_eq));  // open: gt, lt
  flip_flop_condicao flip_flop_condicao_2 (
    .Clock(comparator_2_eq), .Enable(1'b1), .Clear(1'b0), .valor_retorno(4'b0000), .valor_max__1(4'b0010),
    .valor_saida(flip_flop_condicao_2_valor_saida));  // open: Preset
  Comparator #(.width(4)) comparator_3 (
    .a(flip_flop_condicao_2_valor_saida), .b(4'b0000), .eq(comparator_3_eq));  // open: gt, lt
  and and_2 (and_2_out, comparator_3_eq, ~endA_2, ~endB_2);  // AND_Gate
  verificador_jogador verificador_jogador_1 (.A(endA_2), .B(endB_2), .out_3(verificador_jogador_1_out_3));
  not not_1 (Jogador_A, Jogador_B);
  or or_1 (Jogador_B, and_2_out, verificador_jogador_1_out_3);
  Comparator #(.width(4)) comparator_4 (
    .a(flip_flop_condicao_1_valor_saida), .b(4'b0000), .eq(comparator_4_eq));  // open: gt, lt
  Comparator #(.width(4)) comparator_5 (
    .a(flip_flop_condicao_1_valor_saida), .b(4'b0001), .eq(comparator_5_eq));  // open: gt, lt
  Comparator #(.width(4)) comparator_6 (
    .a(flip_flop_condicao_1_valor_saida), .b(4'b0000), .eq(Chutando_X));  // open: gt, lt
  Multiplexer #(.width(4)) multiplexer_1 (.in0(a), .in1(b), .out(multiplexer_1_out), .sel(Jogador_B));  // open: en
  and and_3 (and_3_out, comparator_4_eq, chutar);
  Hex_Digit_Display hex_digit_display_2 (.value(register_1_q));  // open: dp
  LED u_Chutando_X (.in(Chutando_X));
  Multiplexer #(.width(4)) multiplexer_2 (.in0(a), .in1(b), .out(multiplexer_2_out), .sel(Jogador_B));  // open: en
  Register #(.width(4)) register_1 (.D(multiplexer_1_out), .Q(register_1_q), .clk(and_3_out));  // open: en, clr
  and and_4 (and_4_out, chutar, comparator_5_eq);
  Comparator #(.width(4)) comparator_7 (
    .a(flip_flop_condicao_1_valor_saida), .b(4'b0001), .eq(Chutando_Y));  // open: gt, lt
  Register #(.width(4)) register_2 (.D(multiplexer_2_out), .Q(register_2_q), .clk(and_4_out));  // open: en, clr
  Hex_Digit_Display hex_digit_display_3 (.value(register_2_q));  // open: dp
  LED u_Chutando_Y (.in(Chutando_Y));
  and and_5 (and_5_out, comparator_2_eq, Acertou);
  Adder #(.width(4)) adder_1 (.a(register_1_q), .b(register_2_q), .out(adder_1_out));  // open: cin, cout
  numero_negativo numero_negativo_1 (
    .Entrada_3(register_1_q[3]), .Entrada_2(register_1_q[2]), .Entrada_1(register_1_q[1]),
    .Entrada_0(register_1_q[0]), .negativo(SX), .\Saída (saidax));  // open: original
  Hex_Digit_Display hex_digit_display_4 (.value(random_1_out));  // open: dp
  Random #(.width(4)) random_1 (.clk(and_5_out), .out(random_1_out));  // open: next, clr
  Random #(.width(4), .seed(8)) random_2 (.clk(and_5_out), .out(random_2_out));  // open: next, clr
  Hex_Digit_Display hex_digit_display_5 (.value(random_2_out));  // open: dp
  numero_negativo numero_negativo_2 (
    .Entrada_3(register_2_q[3]), .Entrada_2(register_2_q[2]), .Entrada_1(register_2_q[1]),
    .Entrada_0(register_2_q[0]), .negativo(SY), .\Saída (saiday));  // open: original
  Adder #(.width(4)) adder_2 (.a(random_1_out), .b(random_2_out), .out(adder_2_out));  // open: cin, cout
  and and_6 (and_6_out, Jogador_A, Acertou);
  and and_7 (and_7_out, Jogador_B, Acertou);
  Comparator #(.width(4)) comparator_8 (
    .a(adder_1_out), .b(adder_2_out), .gt(comparator_8_gt), .eq(comparator_8_eq), .lt(comparator_8_lt));
  flip_flop_condicao flip_flop_condicao_3 (
    .Clock(and_6_out), .Preset(1'b0), .Enable(1'b1), .Clear(1'b0), .valor_retorno(4'b0000),
    .valor_max__1(4'b1111), .valor_saida(PlacarA));
  flip_flop_condicao flip_flop_condicao_4 (
    .Clock(and_7_out), .Preset(1'b0), .Enable(1'b1), .Clear(1'b0), .valor_retorno(4'b0000),
    .valor_max__1(4'b1111), .valor_saida(PlacarB));
  Comparator #(.width(4)) comparator_9 (.a(register_1_q), .b(random_1_out), .eq(comparator_9_eq));  // open: gt, lt
  Comparator #(.width(4)) comparator_10 (.a(register_2_q), .b(random_2_out), .eq(comparator_10_eq));  // open: gt, lt
  Hex_Digit_Display hex_digit_display_6 (.value(PlacarA));  // open: dp
  Hex_Digit_Display hex_digit_display_7 (.value(PlacarB));  // open: dp
  and and_8 (and_8_out, comparator_9_eq, comparator_10_eq);
  and and_9 (MAIOR, comparator_1_eq, comparator_8_gt);
  LED A___B (.in(MAIOR));
  LED A____B (.in(IGUAL));
  and and_10 (IGUAL, comparator_1_eq, comparator_8_eq);
  and and_11 (MENOR, comparator_1_eq, comparator_8_lt);
  LED A___B_2 (.in(MENOR));
  and and_12 (Acertou, and_8_out, IGUAL);
  Comparator #(.width(4)) comparator_11 (.a(PlacarA), .b(4'b1111), .eq(A_Venceu));  // open: gt, lt
  Comparator #(.width(4)) comparator_12 (.a(PlacarA), .b(PlacarB), .eq(comparator_12_eq));  // open: gt, lt
  Comparator #(.width(4)) comparator_13 (.a(PlacarB), .b(4'b1111), .eq(B_venceu));  // open: gt, lt
  and and_13 (Empate, EndA, ~\teste_1_saída , comparator_12_eq, EndB);  // AND_Gate
  TESTE teste_1 (.Start(start), .\Saída (\teste_1_saída ));
  or or_2 (Fim_de_jogo, A_Venceu, Empate, B_venceu);
endmodule

module flip_flop_condicao (
  input  Clock,
  input  Preset,
  input  Enable,
  input  Clear,
  input  [3:0] valor_retorno,
  input  [3:0] valor_max__1,
  output [3:0] valor_saida
);

  wire comparator_1_eq;
  wire [3:0] adder_1_out, multiplexer_1_out;

  Hex_Digit_Display hex_digit_display_1 (.value(valor_saida));  // open: dp
  Flip_Flop_SR flip_flop_sr_1 (
    .S_R(multiplexer_1_out[3]), .Clock(Clock), .Preset(Preset), .Enable(Enable), .Clear(Clear),
    .out_6(valor_saida[3]));
  Flip_Flop_SR flip_flop_sr_2 (
    .S_R(multiplexer_1_out[2]), .Clock(Clock), .Preset(Preset), .Enable(Enable), .Clear(Clear),
    .out_6(valor_saida[2]));
  Flip_Flop_SR flip_flop_sr_3 (
    .S_R(multiplexer_1_out[1]), .Clock(Clock), .Preset(Preset), .Enable(Enable), .Clear(Clear),
    .out_6(valor_saida[1]));
  Multiplexer #(.width(4)) multiplexer_1 (
    .in0(adder_1_out), .in1(valor_retorno), .out(multiplexer_1_out), .sel(comparator_1_eq));  // open: en
  Flip_Flop_SR flip_flop_sr_4 (
    .S_R(multiplexer_1_out[0]), .Clock(Clock), .Preset(Preset), .Enable(Enable), .Clear(Clear),
    .out_6(valor_saida[0]));
  Hex_Digit_Display hex_digit_display_2 (.value(adder_1_out));  // open: dp
  Adder #(.width(4)) adder_1 (.a(valor_saida), .b(4'b0001), .out(adder_1_out));  // open: cin, cout
  Comparator #(.width(4)) comparator_1 (.a(adder_1_out), .b(valor_max__1), .eq(comparator_1_eq));  // open: gt, lt
endmodule

module numero_negativo (
  input  Entrada_3,
  input  Entrada_2,
  input  Entrada_1,
  input  Entrada_0,
  output [3:0] \Saída ,
  output [3:0] original,
  output negativo
);

  wire [3:0] adder_1_out, not_1_out;

  Multiplexer #(.width(4)) multiplexer_1 (
    .in0({Entrada_3, Entrada_2, Entrada_1, Entrada_0}), .in1(adder_1_out), .out(\Saída ), .sel(Entrada_3));  // open: en
  Hex_Digit_Display hex_digit_display_1 (.value(\Saída ));  // open: dp
  assign not_1_out = ~{Entrada_3, Entrada_2, Entrada_1, Entrada_0};  // NOT_Gate not_1, 4 bits wide
  Adder #(.width(4)) adder_1 (.a(not_1_out), .b(4'b0001), .out(adder_1_out));  // open: cin, cout
  LED u_negativo (.in(Entrada_3));

  assign negativo = Entrada_3;
  assign original = {Entrada_3, Entrada_2, Entrada_1, Entrada_0};
endmodule

module cronometro (
  input  Clear,
  input  clkconfig,
  input  Config,
  input  usa,
  input  Start,
  input  uma,
  input  dsa,
  input  uda,
  input  CLOCK,
  output [3:0] DMA,
  output [3:0] UMA_2,
  output [3:0] DSA_2,
  output [3:0] USA_2,
  output ConfigStatus,
  output startGame,
  output EndTime
);

  wire and_3_out, comparator_1_eq, comparator_2_eq, comparator_3_eq, comparator_4_eq, multiplexer_1_out,
       multiplexer_2_out, multiplexer_3_out, multiplexer_4_out, not_1_out, or_1_out, or_2_out, or_3_out,
       or_4_out;
  wire [3:0] and_1_out;

  S_R_Flip_Flop s_r_ff_1 (
    .S(Config), .clk(clkconfig), .R(Start), .Q(ConfigStatus), .Qn(startGame), .en(1'b1));  // open: preset, reset
  Hex_Digit_Display hex_digit_display_1 (.value(DMA));  // open: dp
  Decrementador decrementador_1 (
    .Clock(multiplexer_1_out), .Enable(or_1_out), .Clear(Clear), .valor_retorno(4'b0101), .out_6(DMA));  // open: Preset
  or or_1 (or_1_out, startGame, ConfigStatus);
  Multiplexer multiplexer_1 (.in0(uda), .in1(comparator_1_eq), .out(multiplexer_1_out), .sel(startGame));  // open: en
  Hex_Digit_Display hex_digit_display_2 (.value(UMA_2));  // open: dp
  Decrementador decrementador_2 (
    .Clock(multiplexer_2_out), .Enable(or_2_out), .Clear(Clear), .valor_retorno(4'b1001), .out_6(UMA_2));  // open: Preset
  or or_2 (or_2_out, startGame, ConfigStatus);
  Multiplexer multiplexer_2 (.in0(uma), .in1(comparator_2_eq), .out(multiplexer_2_out), .sel(startGame));  // open: en
  Comparator #(.width(4)) comparator_1 (.a(UMA_2), .b(4'b1001), .eq(comparator_1_eq));  // open: gt, lt
  assign and_1_out = ~DMA & ~UMA_2 & ~DSA_2 & ~USA_2;  // AND_Gate and_1, 4 bits wide
  Hex_Digit_Display hex_digit_display_3 (.value(DSA_2));  // open: dp
  Decrementador decrementador_3 (
    .Clock(multiplexer_3_out), .Enable(or_3_out), .Clear(Clear), .valor_retorno(4'b0101), .out_6(DSA_2));  // open: Preset
  or or_3 (or_3_out, startGame, ConfigStatus);
  Multiplexer multiplexer_3 (.in0(dsa), .in1(comparator_4_eq), .out(multiplexer_3_out), .sel(startGame));  // open: en
  Comparator #(.width(4)) comparator_2 (.a(DSA_2), .b(4'b0101), .eq(comparator_2_eq));  // open: gt, lt
  Comparator #(.width(4)) comparator_3 (.a(and_1_out), .b(4'b1111), .eq(comparator_3_eq));  // open: gt, lt
  and and_2 (EndTime, comparator_3_eq, startGame);
  Hex_Digit_Display hex_digit_display_4 (.value(USA_2));  // open: dp
  Decrementador decrementador_4 (
    .Clock(multiplexer_4_out), .Enable(or_4_out), .Clear(Clear), .valor_retorno(4'b1001), .out_6(USA_2));  // open: Preset
  or or_4 (or_4_out, startGame, ConfigStatus);
  Multiplexer multiplexer_4 (.in0(usa), .in1(and_3_out), .out(multiplexer_4_out), .sel(startGame));  // open: en
  Comparator #(.width(4)) comparator_4 (.a(USA_2), .b(4'b1001), .eq(comparator_4_eq));  // open: gt, lt
  not not_1 (not_1_out, EndTime);
  and and_3 (and_3_out, not_1_out, CLOCK);
endmodule

module verificador_jogador (
  input  A,
  input  B,
  output out_3
);

  and and_1 (out_3, A, ~B);  // AND_Gate
endmodule

module TESTE (
  input  Start,
  output \Saída 
);

  wire comparator_1_eq, flip_flop_sr_1_out_6, multiplexer_1_out;

  Multiplexer multiplexer_1 (.in0(\Saída ), .in1(1'b1), .out(multiplexer_1_out), .sel(comparator_1_eq));  // open: en
  Flip_Flop_SR flip_flop_sr_1 (
    .S_R(multiplexer_1_out), .Clock(Start), .Preset(1'b0), .Enable(1'b1), .Clear(1'b0),
    .out_6(flip_flop_sr_1_out_6));
  Adder #(.width(1)) adder_1 (.a(flip_flop_sr_1_out_6), .b(1'b1), .out(\Saída ));  // open: cin, cout
  Comparator #(.width(1)) comparator_1 (.a(\Saída ), .b(1'b1), .eq(comparator_1_eq));  // open: gt, lt
endmodule
